# Fritzing sketch DiagramBluetooth (saved by Fritzing 0.9.3b)
breadboards: 1

parts:
  Part1 = Arduino Uno (Rev3)  # not connected
  Part2 = Bluetooth Module Breakout - Roving Networks (RN-41)

nets:
  N1: Part2.RESET, Part2.SPICLK, Part2.PIO7, Part2.PIO6, Part2.SPIMOSI
  N2: Part2.PIO5, Part2.PIO3, Part2.PIO2, Part2.UARTCTS, Part2.UARTRTS
